# Fritzing sketch reader_rfid_diagram (saved by Fritzing 0.9.3b)
breadboards: 1

parts:
  Raspberry_Pi_1 = Raspberry Pi 2
  LED = RGB LED (com. anode, rbg) [package="5 mm [THT]"]
  R1 = Resistor [tolerance=±5% resistance=220 package=THT]
  R2 = Resistor [tolerance=±5% resistance=220 package=THT]
  R3 = Resistor [tolerance=±5% resistance=220 package=THT]
  Součástka1 = RFID-RC522-v2

nets (from the schematic view):
  3V3: Raspberry_Pi_1.3V3, Součástka1.3.3V
  N1: Raspberry_Pi_1.GPIO10, Součástka1.MOSI
  N2: Raspberry_Pi_1.GPIO9, Součástka1.MISO
  N3: Raspberry_Pi_1.GPIO11, Součástka1.SCK
  N4: Raspberry_Pi_1.GPIO21, R3.Pin_0
  N5: Raspberry_Pi_1.GPIO20, R2.Pin_0
  N6: Raspberry_Pi_1.GPIO16, R1.Pin_0
  N7: Raspberry_Pi_1.GND, LED.common_anode, Součástka1.RST
  N8: Raspberry_Pi_1.GPIO8, Součástka1.SDA
  N9: Raspberry_Pi_1.GPIO25, Součástka1.GND
  N10: LED.red_cathode, R1.Pin_1
  N11: LED.blue_cathode, R2.Pin_1
  N12: LED.green_cathode, R3.Pin_1

custom parts:
  RFID-RC522-v2: A simple China made RFID-RC522 Reader; do check the pin labels, as this is a MFRC522 based clone.
