# Fritzing sketch rpi_rfid_diagram (saved by Fritzing 0.9.3b)

parts:
  Raspberry_Pi_1 = Raspberry Pi 2
  Součástka1 = RFID-RC522-v2

nets:
  3V3: Raspberry_Pi_1.3V3, Součástka1.3.3V
  N1: Raspberry_Pi_1.GPIO10, Součástka1.MOSI
  N2: Raspberry_Pi_1.GPIO9, Součástka1.MISO
  N3: Raspberry_Pi_1.GPIO11, Součástka1.SCK
  N4: Raspberry_Pi_1.GPIO8, Součástka1.SDA
  N5: Raspberry_Pi_1.GPIO25, Součástka1.RST
  GND: Raspberry_Pi_1.GND, Součástka1.GND

custom parts:
  RFID-RC522-v2: A simple China made RFID-RC522 Reader; do check the pin labels, as this is a MFRC522 based clone.
