# Fritzing sketch rpi_rgb_led_diagram (saved by Fritzing 0.9.3b)
breadboards: 1

parts:
  Raspberry_Pi_1 = Raspberry Pi 2
  LED1 = RGB LED (com. anode, rbg) [package="5 mm [THT]"]
  R1 = Resistor [tolerance=±5% resistance=220 package=THT]
  R2 = Resistor [tolerance=±5% resistance=220 package=THT]
  R3 = Resistor [tolerance=±5% resistance=220 package=THT]

nets:
  N1: Raspberry_Pi_1.GPIO21, R3.Pin_0
  N2: Raspberry_Pi_1.GPIO20, R2.Pin_0
  N3: Raspberry_Pi_1.GPIO16, R1.Pin_0
  N4: Raspberry_Pi_1.GND, LED1.common_anode
  N5: LED1.red_cathode, R1.Pin_1
  N6: LED1.blue_cathode, R2.Pin_1
  N7: LED1.green_cathode, R3.Pin_1
